# Fritzing sketch gps-neo-6m-board-schematic (saved by Fritzing 0.9.3b)

parts:
  GY-GPS6MV2 = SUP500F [package=sup500f]
  Part1 = Arduino Nano (Rev3.0)

nets:
  N1: GY-GPS6MV2.RX-I, Part1.GND
  N2: GY-GPS6MV2.TX-O, Part1.3V3
  N3: GY-GPS6MV2.GND, Part1.D9
  N4: GY-GPS6MV2.VCC, Part1.D8

notes:
  GND: Black
  VCC: Red
  RX: Yellow
  TX: Green
